// Logisim project faculdadelog.circ as structural Verilog: 1 circuit, main circuit main
module main (
  input  A,
  input  B,
  input  C,
  output S
);

  wire and_1_out;

  and and_1 (and_1_out, A, B);
  or or_1 (S, and_1_out, C);
endmodule
